// Logisim project Circuit.circ as structural Verilog: 9 circuits, main circuit 4x4 Multiplier
// HA
module _1_bit_Half_Adder (
  input  x,
  input  y,
  output Carry,
  output Sum
);

  and and_1 (Carry, x, y);
  xor xor_1 (Sum, x, y);
endmodule

module _1_bit_Full_Adder (
  input  X,
  input  Y,
  input  C_in,
  output C_out,
  output Sum
);

  wire n1_bit_half_adder_1_carry, n1_bit_half_adder_1_sum, n1_bit_half_adder_2_carry;

  _1_bit_Half_Adder u_1_bit_half_adder_1 (
    .x(X), .y(Y), .Carry(n1_bit_half_adder_1_carry), .Sum(n1_bit_half_adder_1_sum));
  _1_bit_Half_Adder u_1_bit_half_adder_2 (
    .x(n1_bit_half_adder_1_sum), .y(C_in), .Carry(n1_bit_half_adder_2_carry), .Sum(Sum));
  or or_1 (C_out, n1_bit_half_adder_1_carry, n1_bit_half_adder_2_carry);
endmodule

// Add
module _4_bit_Adder (
  input  [3:0] X,
  input  [3:0] Y,
  input  C_in,
  output C_out,
  output [3:0] Sum
);

  wire FA0_c_out, FA1_c_out, FA2_c_out;

  _1_bit_Full_Adder FA3 (.X(X[3]), .Y(Y[3]), .C_in(FA2_c_out), .C_out(C_out), .Sum(Sum[3]));
  _1_bit_Full_Adder FA2 (.X(X[2]), .Y(Y[2]), .C_in(FA1_c_out), .C_out(FA2_c_out), .Sum(Sum[2]));
  _1_bit_Full_Adder FA1 (.X(X[1]), .Y(Y[1]), .C_in(FA0_c_out), .C_out(FA1_c_out), .Sum(Sum[1]));
  _1_bit_Full_Adder FA0 (.X(X[0]), .Y(Y[0]), .C_in(C_in), .C_out(FA0_c_out), .Sum(Sum[0]));
endmodule

// Mult
module _4x1_Multiplier (
  input  [3:0] x,
  input  y,
  output [3:0] u
);

  and and_1 (u[2], x[2], y);
  and and_2 (u[3], x[3], y);
  and and_3 (u[1], x[1], y);
  and and_4 (u[0], x[0], y);
endmodule

// 4X4
module _4x4_Multiplier (
  input  C_in,
  input  [3:0] A,
  input  [3:0] B,
  output [7:0] Out
);

  wire [2:0] n4x1_multiplier_4_u;
  wire [3:0] n4_bit_adder_2_c_out, n4_bit_adder_3_c_out, n4x1_multiplier_1_u, n4x1_multiplier_2_u,
       n4x1_multiplier_3_u;

  _4x1_Multiplier u_4x1_multiplier_1 (.x(A), .y(B[3]), .u(n4x1_multiplier_1_u));
  _4_bit_Adder u_4_bit_adder_1 (
    .X(n4_bit_adder_2_c_out), .Y(n4x1_multiplier_1_u), .C_in(C_in), .C_out(Out[7]), .Sum(Out[6:3]));
  _4x1_Multiplier u_4x1_multiplier_2 (.x(A), .y(B[2]), .u(n4x1_multiplier_2_u));
  _4_bit_Adder u_4_bit_adder_2 (
    .X(n4_bit_adder_3_c_out), .Y(n4x1_multiplier_2_u), .C_in(C_in), .C_out(n4_bit_adder_2_c_out[3]),
    .Sum({n4_bit_adder_2_c_out[2:0], Out[2]}));
  _4x1_Multiplier u_4x1_multiplier_3 (.x(A), .y(B[1]), .u(n4x1_multiplier_3_u));
  _4_bit_Adder u_4_bit_adder_3 (
    .X({C_in, n4x1_multiplier_4_u}), .Y(n4x1_multiplier_3_u), .C_in(C_in), .C_out(n4_bit_adder_3_c_out[3]),
    .Sum({n4_bit_adder_3_c_out[2:0], Out[1]}));
  _4x1_Multiplier u_4x1_multiplier_4 (.x(A), .y(B[0]), .u({n4x1_multiplier_4_u, Out[0]}));
endmodule

module Add3 (
  input  A3,
  input  A2,
  input  A1,
  input  A0,
  output [3:0] out_5
);

  wire and_1_out, and_2_out, and_3_out, and_4_out, and_5_out, and_6_out, and_7_out, and_8_out, and_9_out,
       and_10_out;

  and and_1 (and_1_out, A2, A0);
  and and_2 (and_2_out, A2, A1);
  and and_3 (and_3_out, A3, A0);
  and and_4 (and_4_out, A2, ~A1, ~A0);  // AND_Gate
  and and_5 (and_5_out, A3, ~A0);  // AND_Gate
  and and_6 (and_6_out, ~A2, A1);  // AND_Gate
  and and_7 (and_7_out, A1, A0);
  and and_8 (and_8_out, A3, ~A0);  // AND_Gate
  and and_9 (and_9_out, ~A3, ~A2, A0);  // AND_Gate
  and and_10 (and_10_out, A2, A1, ~A0);  // AND_Gate
  or or_1 (out_5[3], A3, and_1_out, and_2_out);
  or or_2 (out_5[2], and_3_out, and_4_out);
  or or_3 (out_5[1], and_5_out, and_6_out, and_7_out);
  or or_4 (out_5[0], and_8_out, and_9_out, and_10_out);
endmodule

module Binary_to_BCD_4x8 (
  input  C_in,
  input  [3:0] X,
  output [3:0] Out_1,
  output [3:0] Out_0
);

  Add3 add3_1 (.A3(C_in), .A2(X[3]), .A1(X[2]), .A0(X[1]), .out_5({Out_1[0], Out_0[3:1]}));

  assign Out_0[0] = X[0];
  assign Out_1[3:1] = {3{C_in}};
endmodule

module Binary_to_BCD_8x12 (
  input  C_in,
  input  [7:0] Input,
  output [3:0] Out_2,
  output [3:0] Out_1,
  output [3:0] Out_0
);

  wire [2:0] add3_5_out_5;
  wire [3:0] add3_1_out_5, add3_2_out_5, add3_3_out_5, add3_4_out_5;

  Add3 add3_1 (.A3(C_in), .A2(Input[7]), .A1(Input[6]), .A0(Input[5]), .out_5(add3_1_out_5));
  Add3 add3_2 (.A3(add3_1_out_5[2]), .A2(add3_1_out_5[1]), .A1(add3_1_out_5[0]), .A0(Input[4]), .out_5(add3_2_out_5));
  Add3 add3_3 (.A3(add3_2_out_5[2]), .A2(add3_2_out_5[1]), .A1(add3_2_out_5[0]), .A0(Input[3]), .out_5(add3_3_out_5));
  Add3 add3_4 (.A3(add3_3_out_5[2]), .A2(add3_3_out_5[1]), .A1(add3_3_out_5[0]), .A0(Input[2]), .out_5(add3_4_out_5));
  Add3 add3_5 (
    .A3(C_in), .A2(add3_1_out_5[3]), .A1(add3_2_out_5[3]), .A0(add3_3_out_5[3]),
    .out_5({Out_2[1], add3_5_out_5}));
  Add3 add3_6 (
    .A3(add3_4_out_5[2]), .A2(add3_4_out_5[1]), .A1(add3_4_out_5[0]), .A0(Input[1]),
    .out_5({Out_1[0], Out_0[3:1]}));
  Add3 add3_7 (
    .A3(add3_5_out_5[2]), .A2(add3_5_out_5[1]), .A1(add3_5_out_5[0]), .A0(add3_4_out_5[3]),
    .out_5({Out_2[0], Out_1[3:1]}));

  assign Out_0[0] = Input[0];
  assign Out_2[3:2] = {2{C_in}};
endmodule

module _4x4_Multiplier_with_Display (
  input  [3:0] A,
  input  [3:0] B,
  input  C_in
);

  wire [3:0] Bin_to_BCD_4X8_2_out_0, Bin_to_BCD_4X8_2_out_1, Bin_to_BCD_4X8_out_0, Bin_to_BCD_4X8_out_1,
       Bin_to_BCD_8X12_out_0, Bin_to_BCD_8X12_out_1, Bin_to_BCD_8X12_out_2;
  wire [7:0] n4x4_multiplier_1_out;

  Hex_Digit_Display hex_digit_display_1 (.value(Bin_to_BCD_4X8_out_1));  // open: dp
  Binary_to_BCD_4x8 Bin_to_BCD_4X8 (.C_in(C_in), .X(A), .Out_1(Bin_to_BCD_4X8_out_1), .Out_0(Bin_to_BCD_4X8_out_0));
  Hex_Digit_Display hex_digit_display_2 (.value(Bin_to_BCD_4X8_out_0));  // open: dp
  _4x4_Multiplier u_4x4_multiplier_1 (.A(A), .C_in(C_in), .B(B), .Out(n4x4_multiplier_1_out));
  Hex_Digit_Display hex_digit_display_3 (.value(Bin_to_BCD_4X8_2_out_1));  // open: dp
  Hex_Digit_Display hex_digit_display_4 (.value(Bin_to_BCD_4X8_2_out_0));  // open: dp
  Binary_to_BCD_4x8 Bin_to_BCD_4X8_2 (
    .C_in(C_in), .X(B), .Out_1(Bin_to_BCD_4X8_2_out_1), .Out_0(Bin_to_BCD_4X8_2_out_0));
  Binary_to_BCD_8x12 Bin_to_BCD_8X12 (
    .Input(n4x4_multiplier_1_out), .C_in(C_in), .Out_2(Bin_to_BCD_8X12_out_2), .Out_1(Bin_to_BCD_8X12_out_1),
    .Out_0(Bin_to_BCD_8X12_out_0));
  Hex_Digit_Display hex_digit_display_5 (.value(Bin_to_BCD_8X12_out_1));  // open: dp
  Hex_Digit_Display hex_digit_display_6 (.value(Bin_to_BCD_8X12_out_2));  // open: dp
  Hex_Digit_Display hex_digit_display_7 (.value(Bin_to_BCD_8X12_out_0));  // open: dp
endmodule
